// Logisim project 2_Gates.circ as structural Verilog: 2 circuits, main circuit NOT_Gates
module NOT_Gates (
);

  wire CLK_out, not_1_out, not_2_out, not_3_out, pull_resistor_1_node;

  Clock CLK (.out(CLK_out));
  not not_1 (not_1_out, CLK_out);
  Pull_Resistor #(.pull(1)) pull_resistor_1 (.node(pull_resistor_1_node));
  Transistor #(.\type ("n")) transistor_1 (.in(1'b0), .out(pull_resistor_1_node), .gate(CLK_out));
  not not_2 (not_2_out, CLK_out);
  not not_3 (not_3_out, not_1_out);
  LED led_1 (.in(pull_resistor_1_node));
  LED led_2 (.in(not_2_out));
  LED led_3 (.in(not_3_out));
  // Digital_Oscilloscope digital_oscilloscope_1: pin names not known; wires that end beside it: pull_resistor_1_node, not_2_out, not_3_out

  // Notes on the sheet:
  //   Inverter
  //   Buffer
  //   Transistor Inverter
  //   2-1 Inverters
endmodule

module OR_Gates (
  input  RST
);

  wire CLK, or_1_out, or_2_out, or_3_out, or_4_out;
  wire [7:0] counter_1_q;

  Counter counter_1 (.clr(RST), .clk(CLK), .Q(counter_1_q));  // open: load, up, count, D, carry
  Clock u_CLK (.out(CLK));
  Hex_Digit_Display hex_digit_display_1 (.value(counter_1_q[7:4]));  // open: dp
  Hex_Digit_Display hex_digit_display_2 (.value(counter_1_q[3:0]));  // open: dp
  or or_1 (or_1_out, counter_1_q[0], counter_1_q[1]);
  or or_2 (or_2_out, counter_1_q[0], counter_1_q[3]);
  or or_3 (or_3_out, counter_1_q[0], counter_1_q[1], counter_1_q[2]);
  or or_4 (or_4_out, counter_1_q[0], counter_1_q[1], counter_1_q[2], counter_1_q[3]);
  // Digital_Oscilloscope #(.nState(16)) digital_oscilloscope_1: pin names not known; wires that end beside it: CLK, or_1_out, or_2_out, or_3_out, or_4_out

  // Notes on the sheet:
  //   2-2 OR Gates
endmodule
