// Logisim project DigitalComputerElectronics.circ as structural Verilog
module SR_Latch (
);

  wire CLK, nor_1_out, nor_2_out, RST_out, s_r_ff_1_q, s_r_ff_1_qn, s_r_ff_2_q, s_r_ff_2_qn, SET_out;

  Clock clock_1 (.out(CLK));
  Button RST (.out(RST_out));
  Button SET (.out(SET_out));
  nor nor_1 (nor_1_out, RST_out, nor_2_out);
  nor nor_2 (nor_2_out, nor_1_out, SET_out);
  S_R_Flip_Flop s_r_ff_1 (
    .S(SET_out), .R(RST_out), .clk(CLK), .Q(s_r_ff_1_q), .Qn(s_r_ff_1_qn));  // open: reset, preset
  S_R_Flip_Flop s_r_ff_2 (
    .S(SET_out), .clk(CLK), .R(RST_out), .Q(s_r_ff_2_q), .Qn(s_r_ff_2_qn));  // open: preset, reset
  LED Q1 (.in(nor_1_out));
  LED NQ1 (.in(nor_2_out));
  LED Q2 (.in(s_r_ff_1_q));
  LED NQ2 (.in(s_r_ff_1_qn));
  LED Q3 (.in(s_r_ff_2_q));
  LED NQ3 (.in(s_r_ff_2_qn));
endmodule

module D_Latch (
  input  in_1,
  input  in_2
);

  wire and_1_out, and_2_out, and_3_out, and_4_out, nor_1_out, nor_2_out, nor_3_out, nor_4_out, not_1_out,
       RST_out, SET_out;

  Button RST (.out(RST_out));
  and and_1 (and_1_out, RST_out, in_1);
  and and_2 (and_2_out, in_1, SET_out);
  Button SET (.out(SET_out));
  not not_1 (not_1_out, in_2);
  nor nor_1 (nor_1_out, and_1_out, nor_2_out);
  nor nor_2 (nor_2_out, nor_1_out, and_2_out);
  and and_3 (and_3_out, not_1_out, in_1);
  and and_4 (and_4_out, in_1, in_2);
  LED Q1 (.in(nor_1_out));
  LED NQ1 (.in(nor_2_out));
  nor nor_3 (nor_3_out, and_3_out, nor_4_out);
  nor nor_4 (nor_4_out, nor_3_out, and_4_out);
  LED Q3 (.in(nor_3_out));
  LED NQ3 (.in(nor_4_out));

  // Other names for the same wires on the sheet: Enable = in_1

  // Notes on the sheet:
  //   D Latch
  //   S-R Latch with Enable
endmodule

module D_Flip_Flop (
);

  wire CLK, d_ff_1_q, D_out;

  Clock clock_1 (.out(CLK));
  Button D (.out(D_out));
  D_Flip_Flop_part d_ff_1 (.D(D_out), .clk(CLK), .Q(d_ff_1_q));  // open: Qn, preset, reset
  // Digital_Oscilloscope digital_oscilloscope_1: pin names not known; wires that end beside it: D_out, CLK, CLK, D_out, d_ff_1_q
endmodule
